# Fritzing sketch wire-diagram (saved by Fritzing 0.9.5d)
breadboards: 1

parts:
  Part1 = Arduino Uno (Rev3) - ICSP
  U1 = POT [package=pot_alpha_rv16af-20]
  S1 = Pushbutton [package="[THT]"]
  Part2 = OLED Monochrome 128x32 I2C [part_number=931]

nets:
  N1: Part1.A2, U1.S
  N2: Part1.A4/SDA, Part2.SDA
  N3: Part1.A5/SCL, Part2.SCL
  GND: Part1.D2, Part1.GND, U1.A, S1.Pin_1, S1.Pin_2, Part2.VIN, Part2.GND
  N4: Part1.5V, U1.E
  N5: S1.Pin_3, S1.Pin_4

custom parts:
  OLED Monochrome 128x32 I2C: These displays are small, only about 1" diagonal, but very readable due to the high contrast of an OLED display. This display is made of 128x32 individual white OLED pixels, each one is turned on or off by the controller chip. Because the display makes its own light, no backlight is required. This reduces the power required to run the OLED and is why the display has such high contrast; we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
